# Fritzing sketch trafficlight (saved by Fritzing 1.0.2b)
breadboards: 1

parts:
  Mod1 = Raspberry Pi Pico
  R1 = Resistor [tolerance=±5% resistance=220 package="0805 [SMD]"]
  LED1 = smd LED [color="Red (633nm)" package="1206 [SMD]"]
  LED2 = smd LED [color="Yellow (595nm)" package="1206 [SMD]"]
  LED3 = smd LED [color="Green (555nm)" package="1206 [SMD]"]
  R2 = Resistor [tolerance=±5% resistance=220 package="0805 [SMD]"]
  R3 = Resistor [tolerance=±5% resistance=220 package="0805 [SMD]"]
  S1 = Pushbutton [package="[THT]"]

nets:
  N1: Mod1.pin_3, Mod1.pin_8, Mod1.pin_13, Mod1.pin_18, Mod1.pin_23, Mod1.pin_28, Mod1.pin_33, Mod1.pin_38, Mod1.pin_42, LED1.cathode, LED2.cathode, LED3.cathode
  N2: Mod1.pin_16, S1.Pin_1, S1.Pin_2
  N3: Mod1.pin_17, R3.Pin_1
  N4: Mod1.pin_19, R2.Pin_1
  N5: Mod1.pin_20, R1.Pin_1
  N6: Mod1.pin_36, S1.Pin_3, S1.Pin_4
  N7: R1.Pin_0, LED1.anode
  N8: LED2.anode, R2.Pin_0
  N9: LED3.anode, R3.Pin_0

custom parts:
  Raspberry Pi Pico: Raspberry Pi Pico. Based around the RP2040 microcontroller the Pico is a low cost microcontroller device bringing Raspberry Pi quality, cost, and easy of use to the microcontroller space. Jan 2021, Split part in to two versions: tht (this one) and SMD. This one will drill holes for a .1 in header in pcb to allow plugging in the module as well as providing pads to solder the module to the top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
